# Fritzing sketch KRETSSCHEMA (saved by Fritzing 0.9.3b)
breadboards: 1

parts:
  ARDUINO_UNO = Arduino Uno (Rev3)
  SMS = Soil Moisture Sensor
  RIGHT = Pushbutton [package="[THT]"]
  LEFT = Pushbutton [package="[THT]"]
  LCD_16X2_I2C = 24LC04 [package=THT]
  DHT11 = mystery part, 3 pins [chip_label=DHT11]
  R1 = Resistor [tolerance=±5% resistance=10k package=THT]
  R2 = Resistor [tolerance=±5% resistance=10k package=THT]
  DS3231 = Real Time Clock Module - DS1307 RTC Breakout Board
  DHT11_modul = mystery part, 3 pins [chip_label=DHT11]
  LED-strip = mystery part, 4 pins [chip_label=Dotstar]
  IR-sensor = mystery part, 3 pins [chip_label="Luxorparts PIR-sensor"]

nets (from the schematic view):
  N1: ARDUINO_UNO.A2, SMS.SIG
  N2: ARDUINO_UNO.A5/SCL, LCD_16X2_I2C.SCL_-_I2C_Clock, DS3231.SCL
  N3: ARDUINO_UNO.D8, DHT11.pin2
  N4: ARDUINO_UNO.D9_PWM, IR-sensor.pin2
  N5: ARDUINO_UNO.D11_PWM/MOSI, LEFT.Pin_4, R1.Pin_1
  N6: ARDUINO_UNO.D12/MISO, RIGHT.Pin_3, RIGHT.Pin_4, R2.Pin_1
  GND: ARDUINO_UNO.GND, SMS.GND, RIGHT.Pin_2, LEFT.Pin_2, LCD_16X2_I2C.0V, DS3231.GND
  N7: ARDUINO_UNO.A4/SDA, LCD_16X2_I2C.SDA_-_I2C_Data, DS3231.SDA
  N8: ARDUINO_UNO.D5_PWM, LED-strip.pin3
  N9: ARDUINO_UNO.D6_PWM, LED-strip.pin2
  N10: ARDUINO_UNO.D7, DHT11_modul.pin2
  N11: ARDUINO_UNO.5V, R1.Pin_0, DHT11_modul.pin1, LED-strip.pin4, IR-sensor.pin1
  N12: SMS.VCC, LCD_16X2_I2C.+V
  N13: DHT11.pin3, DHT11_modul.pin3, LED-strip.pin1, IR-sensor.pin3
  N14: R2.Pin_0, DS3231.5V
